# Fritzing sketch Board (saved by Fritzing 0.9.3b)
perfboards: 1

parts:
  Q1 = Basic FET P-Channel [package="TO220 [THT]"]
  R1 = Resistor [tolerance=±5% resistance=220 package=THT]
  R2 = Resistor [tolerance=±5% resistance=220 package=THT]
  R3 = Resistor [tolerance=±5% resistance=220 package=THT]
  U1 = Voltage Regulator - 5V [package="TO220 [THT]"]
  U2 = ESP32S-HiLetgo [part_number=ESP32S-HiLetgo]
  Bauteil1 = Adafruit MAX31856 Thermocouple Amp [part_number="Adafruit #3263"]
  U3 = Optocoupler [package=THT]
  U4 = Optocoupler [package=THT]
  R4 = Resistor [tolerance=±5% resistance=220 package=THT]
  J3 = female pin header, 7 pins [form="♀ (female)"]
  J4 = female pin header, 5 pins [form="♀ (female)"]
  Q2 = Basic FET N-Channel [package="TO220 [THT]"]
  R5 = Resistor [tolerance=±5% resistance=220 package=THT]
  R6 = Resistor [tolerance=±5% resistance=220 package=THT]
  J5 = female pin header, 3 pins [form="♀ (female)"]
  J2 = Screw terminal - 2 pins [package=THT]

nets:
  N1: Q1.gate, R1.Pin_0, R5.Pin_1
  TIP+: Q1.drain, Bauteil1.THERM+
  24V: Q1.source, R1.Pin_1, U1.input_voltage, U4.Pin_5, J2.pin2
  GND: R2.Pin_0, U1.GND, U2.GND, Bauteil1.GND, U3.Pin_2, U3.Pin_4, U4.Pin_2, J3.pin7, J4.pin5, Q2.source, J2.pin1
  N2: R2.Pin_1, Q2.gate, R6.Pin_0
  HeaterGPIO: R3.Pin_0, U2.GPIO32, R4.Pin_0
  N3: R3.Pin_1, U3.Pin_1
  5V: U1.output_voltage, U2.VIN
  3.3V: U2.3.3, Bauteil1.3.3V, J3.pin6, J4.pin4
  Tip_Switch: U2.GPIO33, J5.pin2
  ROD_CLK: U2.GPIO26, J4.pin1
  ROD_DT: U2.GPIO27, J4.pin2
  ROD_SW: U2.GPIO14, J4.pin3
  OLED_RES: U2.GPIO15, J3.pin3
  OLED_CS: U2.GPIO2, J3.pin1
  OLED_DC: U2.GPIO0, J3.pin2
  MAX_CS: U2.GPIO4, Bauteil1.!CS
  MAX_DRDY: U2.GPIO16, Bauteil1.DRDY
  MAX_SCK/OLED_SCL: U2.GPIO18, Bauteil1.SCK, J3.pin5
  MAX_SDO: U2.GPIO19, Bauteil1.SDO
  MAX_SDI/OLED_SDA: U2.GPIO23, Bauteil1.SDI, J3.pin4
  Tip-: Bauteil1.THERM-, Q2.drain
  N4: U3.Pin_5, R5.Pin_0
  N5: U4.Pin_1, R4.Pin_1
  N6: U4.Pin_4, R6.Pin_1
  Tip_ESD: J5.pin1
  Tip_JC: J5.pin3

custom parts:
  ESP32S-HiLetgo: HiLetgo ESP-WROOM-32 ESP32 ESP-32S Development Board 2.4GHz Dual-Mode WiFi + Bluetooth Dual Cores Microcontroller The ESP32 integrated with Antenna switches, RF Balun, power amplifiers, low-noise amplifiers, filters, and management modules, and the entire solution occupies the least area of PCB. 2.4 GHz Wi-Fi plus Bluetooth dual-mode chip, with TSMC Ultra-low power consumption 40nm technology,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
  Adafruit MAX31856 Thermocouple Amp: Thermocouples are very sensitive, requiring a good amplifier with a cold-compensation reference, as well as calculations to handle any non-linearities. For a long time we've suggested our MAX31855K breakout, which works great but is only for K-type thermocouples. Now we're happy to offer a great new thermocouple amplifier/converter that can handle just about any type of thermocouple, and even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
